# Fritzing sketch roboPlatform (saved by Fritzing 0.9.3b)
breadboards: 1

parts:
  Часть1 = Arduino Nano (Rev3.0)
  VCC1 = Battery
  S1 = Pushbutton [package="[THT]"]
  S4 = Pushbutton [package="[THT]"]
  S5 = Pushbutton [package="[THT]"]
  R1 = Resistor [tolerance=±5% resistance=2.2 package=THT]
  R2 = Resistor [tolerance=±5% resistance=2.2 package=THT]
  R3 = Resistor [tolerance=±5% resistance=2.2 package=THT]
  C1 = Ceramic Capacitor [capacitance=1µF package="100 mil [THT, multilayer]"]
  C2 = Ceramic Capacitor [capacitance=1µF package="100 mil [THT, multilayer]"]
  C3 = Ceramic Capacitor [capacitance=1µF package="100 mil [THT, multilayer]"]
  R4 = Resistor [tolerance=±5% resistance=1.5k package=THT]
  R5 = Resistor [tolerance=±5% resistance=1.5k package=THT]
  R6 = Resistor [tolerance=±5% resistance=1.5k package=THT]
  LCD1 = LCD screen
  MD03A1 = Dual VNH2SP30 Motor Driver [part_number=MD03A]
  M1 = DC Motor
  M2 = DC Motor
  Q1 = NPN-Transistor [package="TO92 [THT]"]
  R7 = Resistor [tolerance=±5% resistance=4.7k package=THT]
  Q2 = NPN-Transistor [package="TO92 [THT]"]
  R8 = Resistor [tolerance=±5% resistance=4.7k package=THT]
  R9 = Resistor [tolerance=±5% resistance=4.7k package=THT]
  R10 = Resistor [tolerance=±5% resistance=4.7k package=THT]
  Часть2 = SRF05 Ultrasonic Rangefinder
  LED1 = LED - 5mm [color="Infrared (940nm)" package="5 mm [THT]"]  # not connected
  LED2 = LED - 5mm [color="Infrared (940nm)" package="5 mm [THT]"]
  LED3 = LED - 5mm [color="Infrared (940nm)" package="5 mm [THT]"]
  LED4 = LED - 5mm [color="Blue (470nm)" package="5 mm [THT]"]
  R11 = Resistor [tolerance=±5% resistance=10k package=THT]
  R12 = Resistor [tolerance=±5% resistance=10k package=THT]
  R13 = Resistor [tolerance=±5% resistance=10k package=THT]
  LED5 = LED - 5mm [color="Blue (470nm)" package="5 mm [THT]"]
  LED6 = LED - 5mm [color="Blue (470nm)" package="5 mm [THT]"]
  R14 = Resistor [tolerance=±5% resistance=100 package=THT]
  R15 = Resistor [tolerance=±5% resistance=100 package=THT]
  R16 = Resistor [tolerance=±5% resistance=100 package=THT]

nets:
  N1: Часть1.D2, R6.Pin_1
  N2: Часть1.D3, R4.Pin_1
  N3: Часть1.D4, R5.Pin_1
  N4: Часть1.D5, LCD1.DB7
  N5: Часть1.D6, MD03A1.2INb#142
  N6: Часть1.D7, MD03A1.2PWM
  N7: Часть1.D8, MD03A1.1INa
  N8: Часть1.D9, MD03A1.PWM
  N9: Часть1.D10, Часть2.Trig
  N10: Часть1.D11/MOSI, Часть2.Echo
  GND: Часть1.GND, VCC1.-, S1.Pin_3, S1.Pin_4, S4.Pin_3, S4.Pin_4, C3.1, MD03A1.GND, Q1.C, Q2.C, Часть2.GND
  5V: Часть1.5V, R9.Pin_1, R10.Pin_1, Часть2.VCC, R11.Pin_0, R12.Pin_0, R13.Pin_0, R14.Pin_0, R15.Pin_0, R16.Pin_0
  N11: Часть1.A5, LCD1.LED-
  N12: Часть1.A4, LCD1.LED+
  N13: Часть1.A2, LED4.anode, R11.Pin_1
  N14: Часть1.A1, R12.Pin_1, LED5.anode
  N15: Часть1.A0, R13.Pin_1, LED6.anode
  N16: VCC1.+, MD03A1.VIN
  N17: S1.Pin_1, S1.Pin_2, R6.Pin_0
  N18: S4.Pin_1, S4.Pin_2, R5.Pin_0
  N19: S5.Pin_1, S5.Pin_2, R4.Pin_0
  N20: R1.Pin_0, C3.0
  N21: R2.Pin_0, C2.0
  N22: R3.Pin_0, C1.0
  N23: MD03A1.1INb, Q1.B, R10.Pin_0
  N24: MD03A1.2INb#143, Q2.B, R9.Pin_0
  N25: MD03A1.OUT_1A, M1.pin_1
  N26: MD03A1.OUT_1B, M1.pin_2
  N27: MD03A1.OUT_2A, M2.pin_1
  N28: MD03A1.OUT_2B, M2.pin_2
  N29: Q1.E, R7.Pin_1
  N30: Q2.E, R8.Pin_1
  N31: LED2.cathode, R15.Pin_1
  N32: LED2.anode, LED5.cathode
  N33: LED3.cathode, R16.Pin_1

notes:
  SDA
  SCL
  подсветка ШИМ
  5V
  7.5V
  right
  centre
  left
  Buttons
  Left
  Centre
  Right
